# Fritzing sketch BTSpeakerESP32 (saved by Fritzing 1.0.1rc)
perfboards: 1

parts:
  YwRobot_Power_Supply1 = YwRobot Breadboard Power Supply [part_number=545043]
  Part1 = Adafruit MAX98357A I2S 3W Class D Amplifier [part_number="Adafruit #3006"]
  Part2 = node32s
  J1 = female pin header, 1 pin [form="♀ (female)"]

nets:
  VIN: YwRobot_Power_Supply1.VCC#5, Part1.VIN, Part2.3.3V
  GND: YwRobot_Power_Supply1.GND#11, Part1.GND, Part2.GND
  N1: YwRobot_Power_Supply1.GND#13, J1.pin1
  N2: Part1.DIN, Part2.IO32
  N3: Part1.BCLK, Part2.IO33
  N4: Part1.LRCLK, Part2.IO25

custom parts:
  YwRobot Breadboard Power Supply: The YwRobot Breadboard Power Supply (MB-V2) has two power rails; they can be 5V or 3V3. Power to the module can be provided through the female USB socket or through the A10 (female) 2.1mm power jack.
  Adafruit MAX98357A I2S 3W Class D Amplifier: Listen to this good news - we now have an all in one digital audio amp breakout board that works incredibly well with the Raspberry Pi! If you're looking for an easy and low cost way to get you digital sound files bumpin' then the MAX08357 I2S Amp Breakout is for you. It takes standard I2S digital audio input and, not only decodes it into analog, but also amplifies it directly into a speaker.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

// code stored in the sketch: SmartHomeRemote.ino

